# Fritzing sketch Aquarius (saved by Fritzing 0.9.2b)
breadboards: 1

parts:
  Led_R = Basic FET N-Channel [package="D2Pak [SMD]"]
  Led_G = Basic FET N-Channel [package="D2Pak [SMD]"]
  Led_B = Basic FET N-Channel [package="D2Pak [SMD]"]
  Fan = Basic FET N-Channel [package="D2Pak [SMD]"]
  IC1 = Voltage Regulator [package=to220-igo]
  C1 = Capacitor [package=cap-pth-small2]
  C2 = Capacitor [package=cap-pth-small2]
  Raspberry_Pi1 = Raspberry Pi B+
  J1 = Power Jack [package=power_jack_slot]
  LED = Header 4 [package=screwterminal-3.5mm-4_lock]
  VENTILATORE = Header 2 [package=screwterminal-3.5mm-2_lock]
  Food = Basic FET N-Channel [package="D2Pak [SMD]"]
  DOSATORE = Header 3 [package=screwterminal-3.5mm-3_lock.007s]
  SONDA_T = Header 3 [package=screwterminal-3.5mm-3_lock.007s]
  R1 = Resistor [tolerance=±5% resistance=4.7k package="0603 [SMD]"]
  DISPLAY = Header 10 [package=1x10-2mm-smd]

nets:
  N1: Led_R.Gate, Raspberry_Pi1.GPIO17
  N2: Led_R.drain, LED.2
  GND: Led_R.source, Led_G.source, Led_B.source, Fan.source, IC1.GND, C1.2, C2.2, Raspberry_Pi1.GND, J1.GND, SONDA_T.3, DISPLAY.10
  N3: Led_G.Gate, Raspberry_Pi1.GPIO18
  N4: Led_G.drain, LED.3
  N5: Led_B.Gate, Raspberry_Pi1.GPIO27
  N6: Led_B.drain, LED.4
  N7: Fan.Gate, Raspberry_Pi1.GPIO26
  N8: Fan.drain, VENTILATORE.2
  N9: IC1.OUT, C1.1, Raspberry_Pi1.5V
  N10: C2.1, J1.PWR, LED.1, VENTILATORE.1, DOSATORE.1
  N11: Raspberry_Pi1.GPIO4, SONDA_T.2, R1.Pin_1
  N12: Raspberry_Pi1.3V3, SONDA_T.1, R1.Pin_0, DISPLAY.9
  N13: Raspberry_Pi1.GPIO10, DISPLAY.4
  N14: Raspberry_Pi1.GPIO11, DISPLAY.3
  N15: Raspberry_Pi1.GPIO5, DISPLAY.5
  N16: Raspberry_Pi1.GPIO6, DISPLAY.7
  N17: Raspberry_Pi1.GPIO13, DISPLAY.8
  N18: Raspberry_Pi1.GPIO12, Food.Gate
  N19: Raspberry_Pi1.GPIO25, DISPLAY.1
  N20: Food.drain, DOSATORE.2
  N21: Food.source, DOSATORE.3
